// Logisim project ALUControl.circ as structural Verilog: 1 circuit, main circuit main
module main (
  input  [4:0] in_1,
  output [2:0] AluOp
);

  wire decoder_1_out0, decoder_1_out1, decoder_1_out4, decoder_1_out7, decoder_1_out11;

  Decoder #(.select(5), .enable("false")) decoder_1 (
    .out0(decoder_1_out0), .out1(decoder_1_out1), .out4(decoder_1_out4), .out5(AluOp[2]),
    .out7(decoder_1_out7), .out11(decoder_1_out11), .sel(in_1));  // open: out2, out3, out6, out8, out9, out10, out12, out13, out14, out15, out16, out17, out18, out19, out20, out21, out22, out23, out24, out25, out26, out27, out28, out29, out30, out31
  nor nor_1 (AluOp[1], decoder_1_out1, decoder_1_out4, AluOp[2], decoder_1_out11);
  or or_1 (AluOp[0], decoder_1_out0, decoder_1_out4, decoder_1_out7, decoder_1_out11);
endmodule
