// Logisim project ConditionControl.circ as structural Verilog: 1 circuit, main circuit main
module main (
  input  [2:0] Cond_ZeroFlag,
  output CondSignal,
  output RegWMemRMemW
);

  wire decoder_1_out2, decoder_1_out5;

  Decoder #(.select(3), .enable("false")) decoder_1 (
    .out2(decoder_1_out2), .out5(decoder_1_out5), .sel(Cond_ZeroFlag));  // open: out0, out1, out3, out4, out6, out7
  or or_1 (CondSignal, decoder_1_out2, decoder_1_out5);
  nor nor_1 (RegWMemRMemW, decoder_1_out2, decoder_1_out5);
endmodule
