// Logisim project DataBath.circ as structural Verilog: 1 circuit, main circuit main
// DataBath
module main (
  input  SF,
  output [4:0] op,
  output out_3,
  output [23:0] out_4,
  output [1:0] co,
  output [23:0] out_6,
  output Write_prime_back,
  output mem_write,
  output mem_read,
  output [1:0] RegDest_prime,
  output ExpOp,
  output [2:0] out_12,
  output [1:0] out_13
);

  wire alu_1_zero_flag, and_1_out, and_2_out, and_3_out, clk_out, controlled_buffer_1_out, main_1_condsignal,
       main_1_regwmemrmemw, main_2_out_3, main_7_aluen, main_7_alusrc, main_7_memr, main_7_memw, main_7_regw,
       not_1_out, not_2_out, store;
  wire [1:0] main_3_pcsrc, multiplexer_2_out;
  wire [2:0] multiplexer_4_out, multiplexer_5_out;
  wire [22:7] ram_1_data;
  wire [23:0] adder_1_out, adder_2_out, adder_3_out, alu_1_output, bit_extender_1_out, main_4_out1,
       main_4_out2, main_5_out_3, multiplexer_1_out, multiplexer_3_out, multiplexer_6_out, PC_q, ram_2_data;

  Clock clk (.out(clk_out));
  ConditionControl_main main_1 (
    .Cond_ZeroFlag({co, out_3}), .CondSignal(main_1_condsignal), .RegWMemRMemW(main_1_regwmemrmemw));
  Multiplexer #(.select(2), .width(24), .enable("false")) multiplexer_1 (
    .in0(main_4_out1), .in1(adder_1_out), .in2(adder_3_out), .in3(adder_2_out), .out(multiplexer_1_out),
    .sel(multiplexer_2_out));
  Multiplexer #(.width(2), .enable("false")) multiplexer_2 (
    .in0(main_3_pcsrc), .in1(2'b01), .out(multiplexer_2_out), .sel(main_1_condsignal));
  Adder #(.width(24)) adder_1 (.a(24'h1), .b(PC_q), .out(adder_1_out));  // open: cin, cout
  Register #(.width(24)) PC (.D(multiplexer_1_out), .Q(PC_q), .clk(clk_out));  // open: en, clr
  Multiplexer #(.select(2), .width(24), .enable("false")) multiplexer_3 (
    .in0(adder_1_out), .in1(out_4), .in2({SF, ram_1_data, {7{1'b0}}}), .out(multiplexer_3_out), .sel(out_13));  // open: in3
  RAM #(.addrWidth(24), .dataWidth(24)) ram_1 (
    .addr(PC_q), .data({co, op, SF, ram_1_data}));  // open: sel, clk, ld, clr
  ZeroFlagset_main main_2 (.in_2(op), .in_1(SF), .out_3(main_2_out_3));
  nand nand_1 (store, op[3], op[1]);
  Multiplexer #(.width(3), .enable("false")) multiplexer_4 (
    .in0(ram_1_data[22:20]), .in1(ram_1_data[16:14]), .out(multiplexer_4_out), .sel(store));
  Multiplexer #(.select(2), .width(3), .enable("false")) multiplexer_5 (
    .in0(ram_1_data[22:20]), .in1(ram_1_data[22:20]), .in2(3'b111), .in3(3'b001), .out(multiplexer_5_out),
    .sel(RegDest_prime));
  and and_1 (and_1_out, main_1_regwmemrmemw, main_7_regw);
  PcSrc_main main_3 (.PcSrc(main_3_pcsrc), .in_1(op), .in_2(out_3));
  regFile_main main_4 (
    .Write_Data(multiplexer_3_out), .reg1(ram_1_data[19:17]), .reg2(multiplexer_4_out), .CLK(clk_out),
    .OUT1(main_4_out1), .OUT2(main_4_out2), .WR_en(and_1_out), .in_1(multiplexer_5_out));  // open: out_8
  extender_main main_5 (.in_1(ram_1_data[16:7]), .expOp(ExpOp), .out_3(main_5_out_3));
  Adder #(.width(24)) adder_2 (.a(main_5_out_3), .b(PC_q), .out(adder_2_out));  // open: cin, cout
  assign bit_extender_1_out = {{7{1'b0}}, {SF, ram_1_data}};  // Bit_Extender bit_extender_1
  assign controlled_buffer_1_out = main_2_out_3 ? alu_1_zero_flag : 1'bz;  // Controlled_Buffer controlled_buffer_1
  and and_2 (and_2_out, main_2_out_3, and_3_out);
  Multiplexer #(.width(24), .enable("false")) multiplexer_6 (
    .in0(main_4_out2), .in1(main_5_out_3), .out(multiplexer_6_out), .sel(main_7_alusrc));
  Register #(.width(1)) register_1 (
    .D(controlled_buffer_1_out), .en(and_2_out), .Q(out_3), .clk(not_1_out));  // open: clr
  not not_1 (not_1_out, clk_out);
  and and_3 (and_3_out, main_1_regwmemrmemw, main_7_aluen);
  ALUControl_main main_6 (.AluOp(out_12), .in_1(op));
  ALU alu_1 (
    .Rs(main_4_out1), .Rt(multiplexer_6_out), .ALUop(out_12), .Zero_flag(alu_1_zero_flag),
    .Output(alu_1_output), .ALUen(and_3_out));
  Adder #(.width(24)) adder_3 (.a(PC_q), .b(bit_extender_1_out), .out(adder_3_out));  // open: cin, cout
  and and_4 (mem_write, main_1_regwmemrmemw, main_7_memw);
  MainControl_main main_7 (
    .in_1(op), .RegW(main_7_regw), .RegDstS1(RegDest_prime[1]), .RegDstS0(RegDest_prime[0]),
    .AluSrc(main_7_alusrc), .MemW(main_7_memw), .MemR(main_7_memr), .WBdata(Write_prime_back),
    .ALUen(main_7_aluen), .ExtenderOP(ExpOp), .ChoseWritebackS1(out_13[1]), .ChoseWritebackS0(out_13[0]));
  not not_2 (not_2_out, clk_out);
  RAM #(.addrWidth(24), .dataWidth(24), .bus("separate")) ram_2 (
    .addr(alu_1_output), .din(main_4_out2), .data(ram_2_data), .str(mem_write), .sel(1'b1), .clk(not_2_out),
    .ld(mem_read));  // open: clr
  and and_5 (mem_read, main_1_regwmemrmemw, main_7_memr);
  Multiplexer #(.width(24), .enable("false")) multiplexer_7 (
    .in0(alu_1_output), .in1(ram_2_data), .out(out_4), .sel(Write_prime_back));

  // Notes on the sheet:
  //   CondControle
  //   pcSrc
  //   pcControle
  //   LAI24bit
  //   JR 
  //   Write(pc or writeback)
  //   Rd
  //   Rs
  //   ALUsrc
  //   ZeroFlagReg
endmodule
