// Logisim project MainControl.circ as structural Verilog: 1 circuit, main circuit main
module main (
  input  [4:0] in_1,
  output RegW,
  output RegDstS1,
  output RegDstS0,
  output AluSrc,
  output MemW,
  output MemR,
  output WBdata,
  output ALUen,
  output ExtenderOP,
  output ChoseWritebackS1,
  output ChoseWritebackS0
);

  wire decoder_1_out2, decoder_1_out5, decoder_1_out6, decoder_1_out7, decoder_1_out8, decoder_1_out9,
       decoder_1_out11, decoder_1_out12, decoder_1_out13;

  Decoder #(.select(5), .enable("false")) decoder_1 (
    .out2(decoder_1_out2), .out5(decoder_1_out5), .out6(decoder_1_out6), .out7(decoder_1_out7),
    .out8(decoder_1_out8), .out9(decoder_1_out9), .out10(MemW), .out11(decoder_1_out11),
    .out12(decoder_1_out12), .out13(decoder_1_out13), .out14(ChoseWritebackS1), .sel(in_1));  // open: out0, out1, out3, out4, out15, out16, out17, out18, out19, out20, out21, out22, out23, out24, out25, out26, out27, out28, out29, out30, out31
  nor nor_1 (RegW, decoder_1_out5, decoder_1_out6, MemW, decoder_1_out11, decoder_1_out12);
  or or_1 (RegDstS1, decoder_1_out13, ChoseWritebackS1);
  nor nor_2 (RegDstS0, decoder_1_out7, decoder_1_out8, decoder_1_out9, MemW, ChoseWritebackS1);
  or or_2 (AluSrc, decoder_1_out7, decoder_1_out8, decoder_1_out9, MemW);
  or or_3 (MemR, decoder_1_out2, decoder_1_out9);
  nor nor_3 (ALUen, decoder_1_out6, decoder_1_out13, ChoseWritebackS1);
  or or_4 (ExtenderOP, MemW, decoder_1_out9, ChoseWritebackS1);
  nor nor_4 (ChoseWritebackS0, decoder_1_out13, ChoseWritebackS1);

  assign WBdata = MemR;
endmodule
