// Logisim project ZeroFlagset.circ as structural Verilog: 1 circuit, main circuit main
module main (
  input  in_1,
  input  [4:0] in_2,
  output out_3
);

  wire and_1_out, and_2_out, and_3_out, and_4_out, not_1_out, not_2_out, not_3_out, not_4_out, not_5_out,
       not_6_out, not_7_out, not_8_out, not_9_out;

  not not_1 (not_1_out, in_2[4]);
  not not_2 (not_2_out, in_2[3]);
  not not_3 (not_3_out, in_2[1]);
  not not_4 (not_4_out, in_2[0]);
  not not_5 (not_5_out, in_2[4]);
  not not_6 (not_6_out, in_2[3]);
  not not_7 (not_7_out, in_2[1]);
  not not_8 (not_8_out, in_2[4]);
  not not_9 (not_9_out, in_2[2]);
  and and_1 (and_1_out, not_1_out, not_2_out, in_2[2], not_3_out, not_4_out);
  and and_2 (and_2_out, not_5_out, not_6_out, in_2[2], not_7_out, in_2[0]);
  and and_3 (and_3_out, in_2[3], not_8_out, in_2[1], in_2[0], not_9_out);
  and and_4 (and_4_out, in_1, and_1_out);
  or or_1 (out_3, and_4_out, and_3_out, and_2_out);
endmodule
