// Logisim project alu (1).circ as structural Verilog: 1 circuit, main circuit ALU
module ALU (
  input  [23:0] Rs,
  input  [23:0] Rt,
  input  [2:0] ALUop,
  input  ALUen,
  output Zero_flag,
  output [23:0] Output
);

  wire comparator_1_lt, not_1_out;
  wire [23:0] adder_1_out, and_1_out, bit_extender_1_out, multiplexer_1_out, subtractor_1_out;

  Comparator #(.width(24)) comparator_1 (.a(Rs), .b(Rt), .lt(comparator_1_lt));  // open: gt, eq
  not not_1 (not_1_out, comparator_1_lt);
  Subtractor #(.width(24)) subtractor_1 (.a(Rs), .b(Rt), .out(subtractor_1_out));  // open: bin, bout
  Adder #(.width(24)) adder_1 (.a(Rs), .b(Rt), .out(adder_1_out), .cin(1'b0));  // open: cout
  assign and_1_out = Rs & Rt;  // AND_Gate and_1, 24 bits wide
  assign bit_extender_1_out = {{23{1'b0}}, not_1_out};  // Bit_Extender bit_extender_1
  Multiplexer #(.width(24)) multiplexer_1 (
    .in0(Rs), .in1(Rt), .out(multiplexer_1_out), .sel(comparator_1_lt), .en(ALUen));
  Multiplexer #(.select(3), .width(24)) multiplexer_2 (
    .in0(multiplexer_1_out), .in1(subtractor_1_out), .in2(adder_1_out), .in3(and_1_out),
    .in4(bit_extender_1_out), .out(Output), .sel(ALUop), .en(ALUen));  // open: in5, in6, in7
  nor nor_1 (Zero_flag, Output[0], Output[1], Output[2], Output[3], Output[4], Output[5], Output[6], Output[7], Output[8], Output[9], Output[10], Output[11], Output[12], Output[13], Output[14], Output[15], Output[16], Output[17], Output[18], Output[19], Output[20], Output[21], Output[22], Output[23]);

  // Notes on the sheet:
  //   Add operation
  //   Or operation
  //   And operation
  //   Cas operation
  //   Sub operation
  //   Set zero flag
endmodule
