// Logisim project extender.circ as structural Verilog: 1 circuit, main circuit main
module main (
  input  [9:0] in_1,
  input  expOp,
  output [23:0] out_3
);

  wire [23:0] bit_extender_1_out, bit_extender_2_out;

  assign bit_extender_1_out = {{14{1'b0}}, in_1};  // Bit_Extender bit_extender_1
  assign bit_extender_2_out = {{14{in_1[9]}}, in_1};  // Bit_Extender bit_extender_2
  Multiplexer #(.width(24), .enable("false")) multiplexer_1 (
    .in0(bit_extender_1_out), .in1(bit_extender_2_out), .out(out_3), .sel(expOp));

  // Notes on the sheet:
  //   imm 10 
endmodule
