// Logisim project regFile.circ as structural Verilog: 1 circuit, main circuit main
module main (
  input  [2:0] in_1,
  input  [2:0] reg1,
  input  [2:0] reg2,
  input  WR_en,
  input  [23:0] Write_Data,
  input  CLK,
  output [23:0] OUT1,
  output out_8,
  output [23:0] OUT2
);

  wire and_1_out, and_2_out, and_4_out, and_5_out, and_6_out, and_7_out, decoder_1_out0, decoder_1_out1,
       decoder_1_out2, decoder_1_out3, decoder_1_out4, decoder_1_out5, decoder_1_out6, decoder_1_out7;
  wire [23:0] register_1_q, register_2_q, register_3_q, register_4_q, register_5_q, register_6_q,
       register_7_q;

  Decoder #(.select(3), .disabled(0), .enable("false")) decoder_1 (
    .out0(decoder_1_out0), .out1(decoder_1_out1), .out2(decoder_1_out2), .out3(decoder_1_out3),
    .out4(decoder_1_out4), .out5(decoder_1_out5), .out6(decoder_1_out6), .out7(decoder_1_out7), .sel(in_1));
  and and_1 (and_1_out, decoder_1_out1, WR_en);
  and and_2 (and_2_out, decoder_1_out2, WR_en);
  and and_3 (out_8, decoder_1_out3, WR_en);
  and and_4 (and_4_out, decoder_1_out4, WR_en);
  and and_5 (and_5_out, decoder_1_out5, WR_en);
  and and_6 (and_6_out, decoder_1_out6, WR_en);
  and and_7 (and_7_out, decoder_1_out7, WR_en);
  Register #(.width(24)) register_1 (.D(Write_Data), .en(and_1_out), .Q(register_1_q), .clk(CLK), .clr(1'b0));
  Register #(.width(24)) register_2 (.D(Write_Data), .en(and_2_out), .Q(register_2_q), .clk(CLK), .clr(1'b0));
  Register #(.width(24)) register_3 (.D(Write_Data), .en(out_8), .Q(register_3_q), .clk(CLK), .clr(1'b0));
  Register #(.width(24)) register_4 (.D(Write_Data), .en(and_4_out), .Q(register_4_q), .clk(CLK), .clr(1'b0));
  Register #(.width(24)) register_5 (.D(Write_Data), .en(and_5_out), .Q(register_5_q), .clk(CLK), .clr(1'b0));
  Register #(.width(24)) register_6 (.D(Write_Data), .en(and_6_out), .Q(register_6_q), .clk(CLK), .clr(1'b0));
  Register #(.width(24)) register_7 (.D(Write_Data), .en(and_7_out), .Q(register_7_q), .clk(CLK), .clr(1'b0));
  Multiplexer #(.select(3), .width(24)) multiplexer_1 (
    .in0({24{1'b0}}), .in1(register_1_q), .in2(register_2_q), .in3(register_3_q), .in4(register_4_q),
    .in5(register_5_q), .in6(register_6_q), .in7(register_7_q), .out(OUT2), .sel(reg2), .en(1'b1));
  Multiplexer #(.select(3), .width(24)) multiplexer_2 (
    .in0({24{1'b0}}), .in1(register_1_q), .in2(register_2_q), .in3(register_3_q), .in4(register_4_q),
    .in5(register_5_q), .in6(register_6_q), .in7(register_7_q), .out(OUT1), .sel(reg1), .en(1'b1));
  // AND_Gate and_8 is placed but not wired
endmodule
