// Logisim project alu.circ as structural Verilog: 1 circuit, main circuit main
module main (
  input  [23:0] in_1,
  input  [23:0] in_2,
  input  [2:0] alu_operation,
  input  alu_en,
  output [23:0] Output,
  output Zero_flag,
  output Carry_out
);

  wire adder_1_cout, and_2_out, and_3_out, comparator_1_lt, not_1_out, not_2_out, or_2_out, subtractor_1_bout;
  wire [23:0] adder_1_out, and_1_out, bit_extender_1_out, bit_extender_2_out, multiplexer_2_out,
       multiplexer_3_out, multiplexer_4_out, or_1_out, subtractor_1_out;

  Comparator #(.width(24)) comparator_1 (.a(in_2), .b(in_1), .lt(comparator_1_lt));  // open: gt, eq
  Subtractor #(.width(24)) subtractor_1 (
    .a(in_1), .b(in_2), .out(subtractor_1_out), .bout(subtractor_1_bout));  // open: bin
  Adder #(.width(24)) adder_1 (.a(in_1), .b(in_2), .out(adder_1_out), .cout(adder_1_cout));  // open: cin
  assign or_1_out = in_1 | in_2;  // OR_Gate or_1, 24 bits wide
  assign and_1_out = in_1 & in_2;  // AND_Gate and_1, 24 bits wide
  assign bit_extender_1_out = {{23{1'b0}}, comparator_1_lt};  // Bit_Extender bit_extender_1
  Multiplexer #(.enable("false")) multiplexer_1 (
    .in0(adder_1_cout), .in1(subtractor_1_bout), .out(Carry_out), .sel(alu_operation[0]));
  Multiplexer #(.select(3), .width(24)) multiplexer_2 (
    .in0(bit_extender_1_out), .in1(subtractor_1_out), .in2(adder_1_out), .in3(or_1_out), .in4(and_1_out),
    .out(multiplexer_2_out), .sel(alu_operation), .en(alu_en));  // open: in5, in6, in7
  nor nor_1 (Zero_flag, multiplexer_2_out[0], multiplexer_2_out[1], multiplexer_2_out[2], multiplexer_2_out[3], multiplexer_2_out[4], multiplexer_2_out[5], multiplexer_2_out[6], multiplexer_2_out[7], multiplexer_2_out[8], multiplexer_2_out[9], multiplexer_2_out[10], multiplexer_2_out[11], multiplexer_2_out[12], multiplexer_2_out[13], multiplexer_2_out[14], multiplexer_2_out[15], multiplexer_2_out[16], multiplexer_2_out[17], multiplexer_2_out[18], multiplexer_2_out[19], multiplexer_2_out[20], multiplexer_2_out[21], multiplexer_2_out[22], multiplexer_2_out[23]);
  not not_1 (not_1_out, alu_operation[1]);
  and and_2 (and_2_out, alu_operation[0], not_1_out, alu_operation[2]);
  not not_2 (not_2_out, alu_operation[2]);
  Multiplexer #(.width(24)) multiplexer_3 (
    .in0(in_1), .in1(in_2), .out(multiplexer_3_out), .sel(Carry_out), .en(and_2_out));
  Multiplexer #(.width(24), .enable("false")) multiplexer_4 (
    .in0(multiplexer_3_out), .in1(bit_extender_2_out), .out(multiplexer_4_out), .sel(and_3_out));
  assign bit_extender_2_out = {{23{1'b0}}, Carry_out};  // Bit_Extender bit_extender_2
  Multiplexer #(.width(24), .enable("false")) multiplexer_5 (
    .in0(multiplexer_2_out), .in1(multiplexer_4_out), .out(Output), .sel(or_2_out));
  or or_2 (or_2_out, and_2_out, and_3_out);
  and and_3 (and_3_out, alu_operation[0], not_1_out, not_2_out);
endmodule
